// Logisim project Projet1.circ as structural Verilog: 2 circuits, main circuit NOR_NAND
module NOR_NAND (
  input  a,
  input  b,
  output s1,
  output s0
);

  nand nand_1 (s1, a, b);
  nor nor_1 (s0, a, b);
endmodule

module OR_AND (
  input  e1,
  input  e0,
  output s0,
  output s1
);

  wire N0_s0, N0_s1;

  NOR_NAND N0 (.a(e1), .b(e0), .s1(N0_s1), .s0(N0_s0));
  NOR_NAND N1 (.a(N0_s0), .b(N0_s1), .s1(s0), .s0(s1));
endmodule
