// Logisim project Projet4.circ as structural Verilog: 1 circuit, main circuit main
module main (
  input  [3:0] a,
  input  [3:0] b,
  output [3:0] s0,
  output [3:0] s1
);

  assign s0 = ~(a | b);  // NOR_Gate nor_1, 4 bits wide
  assign s1 = a & b;  // AND_Gate and_1, 4 bits wide
endmodule
