// Logisim project Projet5.circ as structural Verilog: 1 circuit, main circuit main
module main (
  input  a,
  input  b,
  output s0,
  output s1,
  output s2
);

  not not_1 (s2, b);

  assign s0 = a;
  assign s1 = b;
endmodule
