// Logisim project Projet7.circ as structural Verilog: 1 circuit, main circuit main
module main (
  input  e0,
  input  e1,
  input  e2,
  input  e3,
  output [1:0] S
);

  // Probe on nothing
  // Probe on nothing
  assign S = {e1, e0} & {e3, e2};  // AND_Gate and_1, 2 bits wide
  // Probe on nothing
endmodule
