// Logisim project ASCII.circ as structural Verilog: 2 circuits, main circuit aff7hexa
module aff7hexa (
  input  e3,
  input  e2,
  input  e1,
  input  e0,
  output a,
  output b,
  output c,
  output d,
  output e,
  output f,
  output g
);

  wire and_1_out, and_2_out, and_3_out, and_4_out, and_5_out, and_6_out, and_7_out, and_8_out, and_9_out,
       and_10_out, and_11_out, and_12_out, and_13_out, and_14_out, and_15_out, and_16_out, and_17_out,
       and_18_out, and_19_out, and_20_out, and_21_out, and_22_out, and_23_out, and_24_out, and_25_out,
       and_26_out, and_27_out, and_28_out, and_29_out, and_30_out, and_31_out, and_32_out, and_33_out,
       and_34_out, and_35_out, and_36_out, and_37_out, not_1_out, not_2_out, not_3_out, not_4_out;

  not not_1 (not_1_out, e3);
  not not_2 (not_2_out, e2);
  not not_3 (not_3_out, e1);
  not not_4 (not_4_out, e0);
  and and_1 (and_1_out, not_2_out, not_4_out);
  and and_2 (and_2_out, not_1_out, e1);
  and and_3 (and_3_out, not_1_out, e2, e0);
  and and_4 (and_4_out, e3, not_2_out, not_3_out);
  and and_5 (and_5_out, e3, not_4_out);
  and and_6 (and_6_out, e2, e1);
  and and_7 (and_7_out, not_1_out, not_3_out, not_4_out);
  and and_8 (and_8_out, not_1_out, e1, e0);
  and and_9 (and_9_out, not_2_out, not_4_out);
  and and_10 (and_10_out, e3, not_3_out, e0);
  and and_11 (and_11_out, not_1_out, not_2_out);
  and and_12 (and_12_out, not_1_out, e2);
  and and_13 (and_13_out, e3, not_2_out);
  and and_14 (and_14_out, not_3_out, e0);
  and and_15 (and_15_out, not_1_out, not_3_out);
  and and_16 (and_16_out, not_1_out, e0);
  and and_17 (and_17_out, not_2_out, not_4_out);
  and and_18 (and_18_out, not_2_out, e1);
  and and_19 (and_19_out, e2, not_3_out, e0);
  and and_20 (and_20_out, e1, not_4_out);
  and and_21 (and_21_out, e3, e2, not_3_out);
  and and_22 (and_22_out, not_2_out, not_4_out);
  and and_23 (and_23_out, e1, not_4_out);
  and and_24 (and_24_out, e3, e1);
  and and_25 (and_25_out, e3, e2);
  and and_26 (and_26_out, not_3_out, not_4_out);
  and and_27 (and_27_out, not_1_out, e2, not_3_out);
  and and_28 (and_28_out, e2, not_4_out);
  and and_29 (and_29_out, e3, not_2_out);
  and and_30 (and_30_out, e3, e1);
  and and_31 (and_31_out, not_2_out, e1);
  and and_32 (and_32_out, e3, not_2_out);
  and and_33 (and_33_out, not_1_out, e2, not_3_out);
  and and_34 (and_34_out, not_1_out, e2, not_4_out);
  and and_35 (and_35_out, e2, not_3_out, e0);
  and and_36 (and_36_out, e1, not_4_out);
  and and_37 (and_37_out, e3, e0);
  or or_1 (a, and_1_out, and_2_out, and_3_out, and_4_out, and_5_out, and_6_out);
  or or_2 (b, and_7_out, and_8_out, and_9_out, and_10_out, and_11_out);
  or or_3 (c, and_12_out, and_13_out, and_14_out, and_15_out, and_16_out);
  or or_4 (d, and_17_out, and_18_out, and_19_out, and_20_out, and_21_out);
  or or_5 (e, and_22_out, and_23_out, and_24_out, and_25_out);
  or or_6 (f, and_26_out, and_27_out, and_28_out, and_29_out, and_30_out);
  or or_7 (g, and_31_out, and_32_out, and_33_out, and_34_out, and_35_out, and_36_out, and_37_out);
endmodule

module ascii (
);

  wire aff7hexa_1_a, aff7hexa_1_b, aff7hexa_1_c, aff7hexa_1_d, aff7hexa_1_e, aff7hexa_1_f, aff7hexa_1_g,
       aff7hexa_2_a, aff7hexa_2_b, aff7hexa_2_c, aff7hexa_2_d, aff7hexa_2_e, aff7hexa_2_f, aff7hexa_2_g,
       button_1_out;
  wire [6:0] keyboard_1_data;

  Keyboard keyboard_1 (.clr(button_1_out), .data(keyboard_1_data));  // open: clk, re, avail
  Button button_1 (.out(button_1_out));
  aff7hexa aff7hexa_1 (
    .e2(keyboard_1_data[6]), .e1(keyboard_1_data[5]), .e0(keyboard_1_data[4]), .a(aff7hexa_1_a),
    .b(aff7hexa_1_b), .c(aff7hexa_1_c), .d(aff7hexa_1_d), .e(aff7hexa_1_e), .f(aff7hexa_1_f), .g(aff7hexa_1_g));  // open: e3
  aff7hexa aff7hexa_2 (
    .e3(keyboard_1_data[3]), .e2(keyboard_1_data[2]), .e1(keyboard_1_data[1]), .e0(keyboard_1_data[0]),
    .a(aff7hexa_2_a), .b(aff7hexa_2_b), .c(aff7hexa_2_c), .d(aff7hexa_2_d), .e(aff7hexa_2_e),
    .f(aff7hexa_2_f), .g(aff7hexa_2_g));
  _7_Segment_Display u_7_segment_display_1 (
    .g(aff7hexa_1_g), .f(aff7hexa_1_f), .a(aff7hexa_1_a), .b(aff7hexa_1_b), .e(aff7hexa_1_e),
    .d(aff7hexa_1_d), .c(aff7hexa_1_c));  // open: dp
  _7_Segment_Display u_7_segment_display_2 (
    .g(aff7hexa_2_g), .f(aff7hexa_2_f), .a(aff7hexa_2_a), .b(aff7hexa_2_b), .e(aff7hexa_2_e),
    .d(aff7hexa_2_d), .c(aff7hexa_2_c));  // open: dp
endmodule
