// Logisim project OctetToBCD.circ as structural Verilog: 3 circuits, main circuit ByteToBCD
module ByteToBCD (
  input  [7:0] E,
  output [3:0] c,
  output [3:0] d,
  output [3:0] u
);

  wire [7:0] divider_1_out;
  wire [7:4] divider_1_rem, divider_2_out, divider_2_rem;

  Divider divider_1 (.a(E), .b(8'ha), .out(divider_1_out), .rem({divider_1_rem, u}));  // open: upper
  Divider divider_2 (.a(divider_1_out), .b(8'ha), .out({divider_2_out, c}), .rem({divider_2_rem, d}));  // open: upper
endmodule

module aff7sec (
  input  e3,
  input  e2,
  input  e1,
  input  e0,
  output a,
  output b,
  output c,
  output d,
  output e,
  output f,
  output g
);

  wire and_1_out, and_2_out, and_3_out, and_4_out, and_5_out, and_6_out, and_7_out, and_8_out, and_9_out,
       and_10_out, and_11_out, and_12_out, and_13_out, and_14_out, and_15_out, and_16_out, and_17_out,
       and_18_out, and_19_out, and_20_out, and_21_out, and_22_out, and_23_out, and_24_out, and_25_out,
       not_1_out, not_2_out, not_3_out, not_4_out;

  not not_1 (not_1_out, e3);
  not not_2 (not_2_out, e2);
  not not_3 (not_3_out, e1);
  not not_4 (not_4_out, e0);
  and and_1 (and_1_out, not_1_out, e1);
  and and_2 (and_2_out, not_1_out, e2, e0);
  and and_3 (and_3_out, e3, not_2_out, not_3_out);
  and and_4 (and_4_out, not_1_out, not_2_out, not_4_out);
  and and_5 (and_5_out, not_1_out, not_2_out);
  and and_6 (and_6_out, not_1_out, not_3_out, not_4_out);
  and and_7 (and_7_out, not_1_out, e1, e0);
  and and_8 (and_8_out, not_2_out, not_3_out);
  and and_9 (and_9_out, not_1_out, e0);
  and and_10 (and_10_out, not_1_out, e2);
  and and_11 (and_11_out, not_2_out, not_3_out);
  and and_12 (and_12_out, not_1_out, not_2_out, e1);
  and and_13 (and_13_out, not_1_out, e2, not_3_out, e0);
  and and_14 (and_14_out, not_1_out, e1, not_4_out);
  and and_15 (and_15_out, not_2_out, not_3_out, not_4_out);
  and and_16 (and_16_out, not_1_out, e1, not_4_out);
  and and_17 (and_17_out, not_2_out, not_3_out, not_4_out);
  and and_18 (and_18_out, not_1_out, e2, not_3_out);
  and and_19 (and_19_out, not_1_out, e2, not_4_out);
  and and_20 (and_20_out, e3, not_2_out, not_3_out);
  and and_21 (and_21_out, not_1_out, not_3_out, not_4_out);
  and and_22 (and_22_out, not_1_out, not_2_out, e1);
  and and_23 (and_23_out, not_1_out, e2, not_3_out);
  and and_24 (and_24_out, e3, not_2_out, not_3_out);
  and and_25 (and_25_out, not_1_out, e1, not_4_out);
  or or_1 (a, and_1_out, and_2_out, and_3_out, and_4_out);
  or or_2 (b, and_5_out, and_6_out, and_7_out, and_8_out);
  or or_3 (c, and_9_out, and_10_out, and_11_out);
  or or_4 (d, and_12_out, and_13_out, and_14_out, and_15_out);
  or or_5 (e, and_16_out, and_17_out);
  or or_6 (f, and_18_out, and_19_out, and_20_out, and_21_out);
  or or_7 (g, and_22_out, and_23_out, and_24_out, and_25_out);
endmodule

module aff_ByteToBCD (
  input  [7:0] E
);

  wire aff7sec_1_a, aff7sec_1_b, aff7sec_1_c, aff7sec_1_d, aff7sec_1_e, aff7sec_1_f, aff7sec_1_g,
       aff7sec_2_a, aff7sec_2_b, aff7sec_2_c, aff7sec_2_d, aff7sec_2_e, aff7sec_2_f, aff7sec_2_g,
       aff7sec_3_a, aff7sec_3_b, aff7sec_3_c, aff7sec_3_d, aff7sec_3_e, aff7sec_3_f, aff7sec_3_g;
  wire [3:0] bytetobcd_1_c, bytetobcd_1_d, bytetobcd_1_u;

  ByteToBCD bytetobcd_1 (.E(E), .c(bytetobcd_1_c), .d(bytetobcd_1_d), .u(bytetobcd_1_u));
  aff7sec aff7sec_1 (
    .e3(bytetobcd_1_c[3]), .e2(bytetobcd_1_c[2]), .e1(bytetobcd_1_c[1]), .e0(bytetobcd_1_c[0]),
    .a(aff7sec_1_a), .b(aff7sec_1_b), .c(aff7sec_1_c), .d(aff7sec_1_d), .e(aff7sec_1_e), .f(aff7sec_1_f),
    .g(aff7sec_1_g));
  aff7sec aff7sec_2 (
    .e3(bytetobcd_1_d[3]), .e2(bytetobcd_1_d[2]), .e1(bytetobcd_1_d[1]), .e0(bytetobcd_1_d[0]),
    .a(aff7sec_2_a), .b(aff7sec_2_b), .c(aff7sec_2_c), .d(aff7sec_2_d), .e(aff7sec_2_e), .f(aff7sec_2_f),
    .g(aff7sec_2_g));
  aff7sec aff7sec_3 (
    .e3(bytetobcd_1_u[3]), .e2(bytetobcd_1_u[2]), .e1(bytetobcd_1_u[1]), .e0(bytetobcd_1_u[0]),
    .a(aff7sec_3_a), .b(aff7sec_3_b), .c(aff7sec_3_c), .d(aff7sec_3_d), .e(aff7sec_3_e), .f(aff7sec_3_f),
    .g(aff7sec_3_g));
  _7_Segment_Display u_7_segment_display_1 (
    .g(aff7sec_1_g), .f(aff7sec_1_f), .a(aff7sec_1_a), .b(aff7sec_1_b), .e(aff7sec_1_e), .d(aff7sec_1_d),
    .c(aff7sec_1_c));  // open: dp
  _7_Segment_Display u_7_segment_display_2 (
    .g(aff7sec_2_g), .f(aff7sec_2_f), .a(aff7sec_2_a), .b(aff7sec_2_b), .e(aff7sec_2_e), .d(aff7sec_2_d),
    .c(aff7sec_2_c));  // open: dp
  _7_Segment_Display u_7_segment_display_3 (
    .g(aff7sec_3_g), .f(aff7sec_3_f), .a(aff7sec_3_a), .b(aff7sec_3_b), .e(aff7sec_3_e), .d(aff7sec_3_d),
    .c(aff7sec_3_c));  // open: dp
endmodule
