// Logisim project TP3.circ as structural Verilog
module demi_add (
  input  a,
  input  b,
  output s,
  output c_out
);

  xor xor_1 (s, a, b);
  and and_1 (c_out, a, b);
endmodule

module full_add_1 (
  input  a,
  input  b,
  input  c_in,
  output c_out,
  output s
);

  wire demi_add_1_c_out, demi_add_1_s, demi_add_2_c_out;

  demi_add demi_add_1 (.a(a), .b(b), .s(demi_add_1_s), .c_out(demi_add_1_c_out));
  demi_add demi_add_2 (.a(demi_add_1_s), .b(c_in), .s(s), .c_out(demi_add_2_c_out));
  or or_1 (c_out, demi_add_1_c_out, demi_add_2_c_out);
endmodule

module full_add_2 (
  input  a,
  input  b,
  input  c_in,
  output s,
  output c_out
);

  wire and_1_out, and_2_out, and_3_out, and_4_out, and_5_out, and_6_out, and_7_out, not_1_out, not_2_out,
       not_3_out;

  not not_1 (not_1_out, a);
  not not_2 (not_2_out, b);
  not not_3 (not_3_out, c_in);
  and and_1 (and_1_out, not_1_out, not_2_out, c_in);
  and and_2 (and_2_out, not_1_out, b, not_3_out);
  and and_3 (and_3_out, a, not_2_out, not_3_out);
  and and_4 (and_4_out, a, b, c_in);
  and and_5 (and_5_out, b, c_in);
  and and_6 (and_6_out, a, c_in);
  and and_7 (and_7_out, a, b);
  or or_1 (s, and_1_out, and_2_out, and_3_out, and_4_out);
  or or_2 (c_out, and_5_out, and_6_out, and_7_out);
endmodule

module add_4_bits (
  input  a0,
  input  a1,
  input  a2,
  input  a3,
  input  b0,
  input  b1,
  input  b2,
  input  b3,
  input  c_in,
  output s1,
  output s2,
  output s0,
  output c_out,
  output s3
);

  wire full_add_1_1_c_out, full_add_1_2_c_out, full_add_1_3_c_out;

  full_add_1 full_add_1_1 (.a(a0), .b(b0), .c_in(c_in), .c_out(full_add_1_1_c_out), .s(s0));
  full_add_1 full_add_1_2 (.a(a1), .b(b1), .c_in(full_add_1_1_c_out), .c_out(full_add_1_2_c_out), .s(s1));
  full_add_1 full_add_1_3 (.a(a2), .b(b2), .c_in(full_add_1_2_c_out), .c_out(full_add_1_3_c_out), .s(s2));
  full_add_1 full_add_1_4 (.a(a3), .b(b3), .c_in(full_add_1_3_c_out), .c_out(c_out), .s(s3));
endmodule

module aff_hexa (
  input  e3,
  input  e2,
  input  e1,
  input  e0,
  output a,
  output b,
  output c,
  output d,
  output e,
  output f,
  output g
);

  wire and_1_out, and_2_out, and_3_out, and_4_out, and_5_out, and_6_out, and_7_out, and_8_out, and_9_out,
       and_10_out, and_11_out, and_12_out, and_13_out, and_14_out, and_15_out, and_16_out, and_17_out,
       and_18_out, and_19_out, and_20_out, and_21_out, and_22_out, and_23_out, and_24_out, and_25_out,
       and_26_out, and_27_out, and_28_out, and_29_out, and_30_out, and_31_out, and_32_out, and_33_out,
       and_34_out, and_35_out, not_1_out, not_2_out, not_3_out, not_4_out;

  not not_1 (not_1_out, e3);
  not not_2 (not_2_out, e2);
  not not_3 (not_3_out, e1);
  not not_4 (not_4_out, e0);
  and and_1 (and_1_out, not_2_out, not_4_out);
  and and_2 (and_2_out, not_1_out, e1);
  and and_3 (and_3_out, not_1_out, e2, e0);
  and and_4 (and_4_out, e3, not_2_out, not_3_out);
  and and_5 (and_5_out, e3, not_4_out);
  and and_6 (and_6_out, e2, e1);
  and and_7 (and_7_out, not_1_out, not_3_out, not_4_out);
  and and_8 (and_8_out, not_1_out, e1, e0);
  and and_9 (and_9_out, not_2_out, not_4_out);
  and and_10 (and_10_out, e3, not_3_out, e0);
  and and_11 (and_11_out, not_1_out, not_2_out);
  and and_12 (and_12_out, not_1_out, e2);
  and and_13 (and_13_out, e3, not_2_out);
  and and_14 (and_14_out, not_3_out, e0);
  and and_15 (and_15_out, not_2_out, not_3_out);
  and and_16 (and_16_out, not_2_out, e0);
  and and_17 (and_17_out, e2, not_3_out, e0);
  and and_18 (and_18_out, not_1_out, not_2_out, not_4_out);
  and and_19 (and_19_out, not_2_out, e1, e0);
  and and_20 (and_20_out, e3, not_3_out);
  and and_21 (and_21_out, e2, e1, not_4_out);
  and and_22 (and_22_out, not_2_out, not_4_out);
  and and_23 (and_23_out, e1, not_4_out);
  and and_24 (and_24_out, e3, e1);
  and and_25 (and_25_out, e3, e2);
  and and_26 (and_26_out, not_3_out, not_4_out);
  and and_27 (and_27_out, not_1_out, e2, not_3_out);
  and and_28 (and_28_out, e2, not_4_out);
  and and_29 (and_29_out, e3, not_2_out);
  and and_30 (and_30_out, e3, e1);
  and and_31 (and_31_out, not_2_out, e1);
  and and_32 (and_32_out, e3, not_2_out);
  and and_33 (and_33_out, not_1_out, e2, not_3_out);
  and and_34 (and_34_out, e1, not_4_out);
  and and_35 (and_35_out, e3, e0);
  or or_1 (a, and_1_out, and_2_out, and_3_out, and_4_out, and_5_out, and_6_out);
  or or_2 (b, and_7_out, and_8_out, and_9_out, and_10_out, and_11_out);
  or or_3 (c, and_12_out, and_13_out, and_14_out, and_15_out, and_16_out);
  or or_4 (d, and_17_out, and_18_out, and_19_out, and_20_out, and_21_out);
  or or_5 (e, and_22_out, and_23_out, and_24_out, and_25_out);
  or or_6 (f, and_26_out, and_27_out, and_28_out, and_29_out, and_30_out);
  or or_7 (g, and_31_out, and_32_out, and_33_out, and_34_out, and_35_out);
endmodule

module add_4_bits_aff_hexa (
  input  [3:0] A,
  input  [3:0] B,
  input  c_in,
  output c_out
);

  wire add_4_bits_1_s0, add_4_bits_1_s1, add_4_bits_1_s2, add_4_bits_1_s3, aff_hexa_1_a, aff_hexa_1_b,
       aff_hexa_1_c, aff_hexa_1_d, aff_hexa_1_e, aff_hexa_1_f, aff_hexa_1_g, aff_hexa_2_a, aff_hexa_2_b,
       aff_hexa_2_c, aff_hexa_2_d, aff_hexa_2_e, aff_hexa_2_f, aff_hexa_2_g, aff_hexa_3_a, aff_hexa_3_b,
       aff_hexa_3_c, aff_hexa_3_d, aff_hexa_3_e, aff_hexa_3_f, aff_hexa_3_g;

  add_4_bits add_4_bits_1 (
    .a0(A[0]), .a1(A[1]), .a2(A[2]), .a3(A[3]), .b0(B[0]), .b1(B[1]), .b2(B[2]), .b3(B[3]), .c_in(c_in),
    .s1(add_4_bits_1_s1), .s2(add_4_bits_1_s2), .s0(add_4_bits_1_s0), .c_out(c_out), .s3(add_4_bits_1_s3));
  aff_hexa aff_hexa_1 (
    .e3(A[3]), .e2(A[2]), .e1(A[1]), .e0(A[0]), .a(aff_hexa_1_a), .b(aff_hexa_1_b), .c(aff_hexa_1_c),
    .d(aff_hexa_1_d), .e(aff_hexa_1_e), .f(aff_hexa_1_f), .g(aff_hexa_1_g));
  aff_hexa aff_hexa_2 (
    .e3(B[3]), .e2(B[2]), .e1(B[1]), .e0(B[0]), .a(aff_hexa_2_a), .b(aff_hexa_2_b), .c(aff_hexa_2_c),
    .d(aff_hexa_2_d), .e(aff_hexa_2_e), .f(aff_hexa_2_f), .g(aff_hexa_2_g));
  _7_Segment_Display u_7_segment_display_1 (
    .g(aff_hexa_1_g), .f(aff_hexa_1_f), .a(aff_hexa_1_a), .b(aff_hexa_1_b), .e(aff_hexa_1_e),
    .d(aff_hexa_1_d), .c(aff_hexa_1_c));  // open: dp
  aff_hexa aff_hexa_3 (
    .e3(add_4_bits_1_s3), .e2(add_4_bits_1_s2), .e1(add_4_bits_1_s1), .e0(add_4_bits_1_s0), .a(aff_hexa_3_a),
    .b(aff_hexa_3_b), .c(aff_hexa_3_c), .d(aff_hexa_3_d), .e(aff_hexa_3_e), .f(aff_hexa_3_f), .g(aff_hexa_3_g));
  _7_Segment_Display u_7_segment_display_2 (
    .g(aff_hexa_2_g), .f(aff_hexa_2_f), .a(aff_hexa_2_a), .b(aff_hexa_2_b), .e(aff_hexa_2_e),
    .d(aff_hexa_2_d), .c(aff_hexa_2_c));  // open: dp
  _7_Segment_Display u_7_segment_display_3 (
    .g(aff_hexa_3_g), .f(aff_hexa_3_f), .a(aff_hexa_3_a), .b(aff_hexa_3_b), .e(aff_hexa_3_e),
    .d(aff_hexa_3_d), .c(aff_hexa_3_c));  // open: dp
endmodule

module add_sous_4_bits (
  input  c_in,
  input  [3:0] a,
  input  [3:0] b,
  output [3:0] s,
  output c_out
);

  wire [3:0] xor_1_out;

  xor xor_1 (xor_1_out[0], c_in, b[0]);
  xor xor_2 (xor_1_out[1], c_in, b[1]);
  xor xor_3 (xor_1_out[2], c_in, b[2]);
  xor xor_4 (xor_1_out[3], c_in, b[3]);
  add_4_bits add_4_bits_1 (
    .a0(a[0]), .a1(a[1]), .a2(a[2]), .a3(a[3]), .b0(xor_1_out[0]), .b1(xor_1_out[1]), .b2(xor_1_out[2]),
    .b3(xor_1_out[3]), .c_in(c_in), .s1(s[1]), .s2(s[2]), .s0(s[0]), .c_out(c_out), .s3(s[3]));
endmodule

module add_sous_4_bits_aff_hexa (
  input  c_in,
  input  [3:0] A,
  input  [3:0] B,
  output c_out
);

  wire aff_hexa_1_a, aff_hexa_1_b, aff_hexa_1_c, aff_hexa_1_d, aff_hexa_1_e, aff_hexa_1_f, aff_hexa_1_g,
       aff_hexa_2_a, aff_hexa_2_b, aff_hexa_2_c, aff_hexa_2_d, aff_hexa_2_e, aff_hexa_2_f, aff_hexa_2_g,
       aff_hexa_3_a, aff_hexa_3_b, aff_hexa_3_c, aff_hexa_3_d, aff_hexa_3_e, aff_hexa_3_f, aff_hexa_3_g;
  wire [3:0] add_sous_4_bits_1_s;

  add_sous_4_bits add_sous_4_bits_1 (.c_in(c_in), .a(A), .b(B), .s(add_sous_4_bits_1_s), .c_out(c_out));
  aff_hexa aff_hexa_1 (
    .e3(A[3]), .e2(A[2]), .e1(A[1]), .e0(A[0]), .a(aff_hexa_1_a), .b(aff_hexa_1_b), .c(aff_hexa_1_c),
    .d(aff_hexa_1_d), .e(aff_hexa_1_e), .f(aff_hexa_1_f), .g(aff_hexa_1_g));
  aff_hexa aff_hexa_2 (
    .e3(B[3]), .e2(B[2]), .e1(B[1]), .e0(B[0]), .a(aff_hexa_2_a), .b(aff_hexa_2_b), .c(aff_hexa_2_c),
    .d(aff_hexa_2_d), .e(aff_hexa_2_e), .f(aff_hexa_2_f), .g(aff_hexa_2_g));
  _7_Segment_Display u_7_segment_display_1 (
    .g(aff_hexa_1_g), .f(aff_hexa_1_f), .a(aff_hexa_1_a), .b(aff_hexa_1_b), .e(aff_hexa_1_e),
    .d(aff_hexa_1_d), .c(aff_hexa_1_c));  // open: dp
  aff_hexa aff_hexa_3 (
    .e3(add_sous_4_bits_1_s[3]), .e2(add_sous_4_bits_1_s[2]), .e1(add_sous_4_bits_1_s[1]),
    .e0(add_sous_4_bits_1_s[0]), .a(aff_hexa_3_a), .b(aff_hexa_3_b), .c(aff_hexa_3_c), .d(aff_hexa_3_d),
    .e(aff_hexa_3_e), .f(aff_hexa_3_f), .g(aff_hexa_3_g));
  _7_Segment_Display u_7_segment_display_2 (
    .g(aff_hexa_2_g), .f(aff_hexa_2_f), .a(aff_hexa_2_a), .b(aff_hexa_2_b), .e(aff_hexa_2_e),
    .d(aff_hexa_2_d), .c(aff_hexa_2_c));  // open: dp
  _7_Segment_Display u_7_segment_display_3 (
    .g(aff_hexa_3_g), .f(aff_hexa_3_f), .a(aff_hexa_3_a), .b(aff_hexa_3_b), .e(aff_hexa_3_e),
    .d(aff_hexa_3_d), .c(aff_hexa_3_c));  // open: dp
endmodule

module ByteToBCD (
  input  [7:0] E,
  output [3:0] c,
  output [3:0] d,
  output [3:0] u
);

  wire [7:0] divider_1_out;
  wire [7:4] divider_1_rem, divider_2_out, divider_2_rem;

  Divider divider_1 (.a(E), .b(8'ha), .out(divider_1_out), .rem({divider_1_rem, u}));  // open: upper
  Divider divider_2 (.a(divider_1_out), .b(8'ha), .out({divider_2_out, c}), .rem({divider_2_rem, d}));  // open: upper
endmodule

module add_8_bits (
  input  [7:0] A,
  input  [7:0] B,
  output c1,
  output c2
);

  wire aff_hexa_1_a, aff_hexa_1_b, aff_hexa_1_c, aff_hexa_1_d, aff_hexa_1_e, aff_hexa_1_f, aff_hexa_1_g,
       aff_hexa_2_a, aff_hexa_2_b, aff_hexa_2_c, aff_hexa_2_d, aff_hexa_2_e, aff_hexa_2_f, aff_hexa_2_g,
       aff_hexa_3_a, aff_hexa_3_b, aff_hexa_3_c, aff_hexa_3_d, aff_hexa_3_e, aff_hexa_3_f, aff_hexa_3_g,
       aff_hexa_4_a, aff_hexa_4_b, aff_hexa_4_c, aff_hexa_4_d, aff_hexa_4_e, aff_hexa_4_f, aff_hexa_4_g,
       aff_hexa_5_a, aff_hexa_5_b, aff_hexa_5_c, aff_hexa_5_d, aff_hexa_5_e, aff_hexa_5_f, aff_hexa_5_g,
       aff_hexa_6_a, aff_hexa_6_b, aff_hexa_6_c, aff_hexa_6_d, aff_hexa_6_e, aff_hexa_6_f, aff_hexa_6_g,
       aff_hexa_7_a, aff_hexa_7_b, aff_hexa_7_c, aff_hexa_7_d, aff_hexa_7_e, aff_hexa_7_f, aff_hexa_7_g,
       aff_hexa_8_a, aff_hexa_8_b, aff_hexa_8_c, aff_hexa_8_d, aff_hexa_8_e, aff_hexa_8_f, aff_hexa_8_g,
       aff_hexa_9_a, aff_hexa_9_b, aff_hexa_9_c, aff_hexa_9_d, aff_hexa_9_e, aff_hexa_9_f, aff_hexa_9_g;
  wire [3:0] bytetobcd_1_c, bytetobcd_1_d, bytetobcd_1_u, bytetobcd_2_c, bytetobcd_2_d, bytetobcd_2_u,
       bytetobcd_3_c, bytetobcd_3_d, bytetobcd_3_u;
  wire [7:0] add_4_bits_2_s3;

  add_4_bits add_4_bits_1 (
    .a0(A[0]), .a1(A[1]), .a2(A[2]), .a3(A[3]), .b0(B[0]), .b1(B[1]), .b2(B[2]), .b3(B[3]),
    .s1(add_4_bits_2_s3[6]), .s2(add_4_bits_2_s3[5]), .s0(add_4_bits_2_s3[7]), .c_out(c1),
    .s3(add_4_bits_2_s3[4]));  // open: c_in
  add_4_bits add_4_bits_2 (
    .a0(A[4]), .a1(A[5]), .a2(A[6]), .a3(A[7]), .b0(B[4]), .b1(B[5]), .b2(B[6]), .b3(B[7]),
    .s1(add_4_bits_2_s3[2]), .s2(add_4_bits_2_s3[1]), .s0(add_4_bits_2_s3[3]), .c_out(c2),
    .s3(add_4_bits_2_s3[0]));  // open: c_in
  ByteToBCD bytetobcd_1 (.E(A), .c(bytetobcd_1_c), .d(bytetobcd_1_d), .u(bytetobcd_1_u));
  ByteToBCD bytetobcd_2 (.E(add_4_bits_2_s3), .c(bytetobcd_2_c), .d(bytetobcd_2_d), .u(bytetobcd_2_u));
  ByteToBCD bytetobcd_3 (.E(B), .c(bytetobcd_3_c), .d(bytetobcd_3_d), .u(bytetobcd_3_u));
  aff_hexa aff_hexa_1 (
    .e3(bytetobcd_1_c[3]), .e2(bytetobcd_1_c[2]), .e1(bytetobcd_1_c[1]), .e0(bytetobcd_1_c[0]),
    .a(aff_hexa_1_a), .b(aff_hexa_1_b), .c(aff_hexa_1_c), .d(aff_hexa_1_d), .e(aff_hexa_1_e),
    .f(aff_hexa_1_f), .g(aff_hexa_1_g));
  aff_hexa aff_hexa_2 (
    .e3(bytetobcd_1_d[3]), .e2(bytetobcd_1_d[2]), .e1(bytetobcd_1_d[1]), .e0(bytetobcd_1_d[0]),
    .a(aff_hexa_2_a), .b(aff_hexa_2_b), .c(aff_hexa_2_c), .d(aff_hexa_2_d), .e(aff_hexa_2_e),
    .f(aff_hexa_2_f), .g(aff_hexa_2_g));
  aff_hexa aff_hexa_3 (
    .e3(bytetobcd_1_u[3]), .e2(bytetobcd_1_u[2]), .e1(bytetobcd_1_u[1]), .e0(bytetobcd_1_u[0]),
    .a(aff_hexa_3_a), .b(aff_hexa_3_b), .c(aff_hexa_3_c), .d(aff_hexa_3_d), .e(aff_hexa_3_e),
    .f(aff_hexa_3_f), .g(aff_hexa_3_g));
  aff_hexa aff_hexa_4 (
    .e3(bytetobcd_3_c[3]), .e2(bytetobcd_3_c[2]), .e1(bytetobcd_3_c[1]), .e0(bytetobcd_3_c[0]),
    .a(aff_hexa_4_a), .b(aff_hexa_4_b), .c(aff_hexa_4_c), .d(aff_hexa_4_d), .e(aff_hexa_4_e),
    .f(aff_hexa_4_f), .g(aff_hexa_4_g));
  aff_hexa aff_hexa_5 (
    .e3(bytetobcd_3_d[3]), .e2(bytetobcd_3_d[2]), .e1(bytetobcd_3_d[1]), .e0(bytetobcd_3_d[0]),
    .a(aff_hexa_5_a), .b(aff_hexa_5_b), .c(aff_hexa_5_c), .d(aff_hexa_5_d), .e(aff_hexa_5_e),
    .f(aff_hexa_5_f), .g(aff_hexa_5_g));
  aff_hexa aff_hexa_6 (
    .e3(bytetobcd_3_u[3]), .e2(bytetobcd_3_u[2]), .e1(bytetobcd_3_u[1]), .e0(bytetobcd_3_u[0]),
    .a(aff_hexa_6_a), .b(aff_hexa_6_b), .c(aff_hexa_6_c), .d(aff_hexa_6_d), .e(aff_hexa_6_e),
    .f(aff_hexa_6_f), .g(aff_hexa_6_g));
  _7_Segment_Display u_7_segment_display_1 (
    .g(aff_hexa_1_g), .f(aff_hexa_1_f), .a(aff_hexa_1_a), .b(aff_hexa_1_b), .e(aff_hexa_1_e),
    .d(aff_hexa_1_d), .c(aff_hexa_1_c));  // open: dp
  _7_Segment_Display u_7_segment_display_2 (
    .g(aff_hexa_4_g), .f(aff_hexa_4_f), .a(aff_hexa_4_a), .b(aff_hexa_4_b), .e(aff_hexa_4_e),
    .d(aff_hexa_4_d), .c(aff_hexa_4_c));  // open: dp
  _7_Segment_Display u_7_segment_display_3 (
    .g(aff_hexa_5_g), .f(aff_hexa_5_f), .a(aff_hexa_5_a), .b(aff_hexa_5_b), .e(aff_hexa_5_e),
    .d(aff_hexa_5_d), .c(aff_hexa_5_c));  // open: dp
  _7_Segment_Display u_7_segment_display_4 (
    .g(aff_hexa_6_g), .f(aff_hexa_6_f), .a(aff_hexa_6_a), .b(aff_hexa_6_b), .e(aff_hexa_6_e),
    .d(aff_hexa_6_d), .c(aff_hexa_6_c));  // open: dp
  _7_Segment_Display u_7_segment_display_5 (
    .g(aff_hexa_2_g), .f(aff_hexa_2_f), .a(aff_hexa_2_a), .b(aff_hexa_2_b), .e(aff_hexa_2_e),
    .d(aff_hexa_2_d), .c(aff_hexa_2_c));  // open: dp
  _7_Segment_Display u_7_segment_display_6 (
    .g(aff_hexa_3_g), .f(aff_hexa_3_f), .a(aff_hexa_3_a), .b(aff_hexa_3_b), .e(aff_hexa_3_e),
    .d(aff_hexa_3_d), .c(aff_hexa_3_c));  // open: dp
  aff_hexa aff_hexa_7 (
    .e3(bytetobcd_2_c[3]), .e2(bytetobcd_2_c[2]), .e1(bytetobcd_2_c[1]), .e0(bytetobcd_2_c[0]),
    .a(aff_hexa_7_a), .b(aff_hexa_7_b), .c(aff_hexa_7_c), .d(aff_hexa_7_d), .e(aff_hexa_7_e),
    .f(aff_hexa_7_f), .g(aff_hexa_7_g));
  aff_hexa aff_hexa_8 (
    .e3(bytetobcd_2_d[3]), .e2(bytetobcd_2_d[2]), .e1(bytetobcd_2_d[1]), .e0(bytetobcd_2_d[0]),
    .a(aff_hexa_8_a), .b(aff_hexa_8_b), .c(aff_hexa_8_c), .d(aff_hexa_8_d), .e(aff_hexa_8_e),
    .f(aff_hexa_8_f), .g(aff_hexa_8_g));
  aff_hexa aff_hexa_9 (
    .e3(bytetobcd_2_u[3]), .e2(bytetobcd_2_u[2]), .e1(bytetobcd_2_u[1]), .e0(bytetobcd_2_u[0]),
    .a(aff_hexa_9_a), .b(aff_hexa_9_b), .c(aff_hexa_9_c), .d(aff_hexa_9_d), .e(aff_hexa_9_e),
    .f(aff_hexa_9_f), .g(aff_hexa_9_g));
  _7_Segment_Display u_7_segment_display_7 (
    .g(aff_hexa_7_g), .f(aff_hexa_7_f), .a(aff_hexa_7_a), .b(aff_hexa_7_b), .e(aff_hexa_7_e),
    .d(aff_hexa_7_d), .c(aff_hexa_7_c));  // open: dp
  _7_Segment_Display u_7_segment_display_8 (
    .g(aff_hexa_8_g), .f(aff_hexa_8_f), .a(aff_hexa_8_a), .b(aff_hexa_8_b), .e(aff_hexa_8_e),
    .d(aff_hexa_8_d), .c(aff_hexa_8_c));  // open: dp
  _7_Segment_Display u_7_segment_display_9 (
    .g(aff_hexa_9_g), .f(aff_hexa_9_f), .a(aff_hexa_9_a), .b(aff_hexa_9_b), .e(aff_hexa_9_e),
    .d(aff_hexa_9_d), .c(aff_hexa_9_c));  // open: dp
endmodule
