// Logisim project tp3.circ as structural Verilog: 6 circuits, main circuit demi_additionneur
module demi_additionneur (
  input  a,
  input  b,
  output somme,
  output retenue
);

  xor xor_1 (somme, a, b);
  and and_1 (retenue, a, b);
endmodule

module additionneur_complet (
  input  a,
  input  b,
  input  c_in,
  output c_out,
  output s
);

  wire demi_additionneur_1_retenue, demi_additionneur_1_somme, demi_additionneur_2_retenue;

  demi_additionneur demi_additionneur_1 (
    .a(a), .b(b), .somme(demi_additionneur_1_somme), .retenue(demi_additionneur_1_retenue));
  demi_additionneur demi_additionneur_2 (
    .a(demi_additionneur_1_somme), .b(c_in), .somme(s), .retenue(demi_additionneur_2_retenue));
  and and_1 (c_out, demi_additionneur_1_retenue, demi_additionneur_2_retenue);
endmodule

module additionneur_complet_table (
  input  a,
  input  b,
  input  c_in,
  output s,
  output c_out
);

  wire and_1_out, and_2_out, and_3_out, and_4_out, and_5_out, and_6_out, and_7_out, not_1_out, not_2_out,
       not_3_out;

  not not_1 (not_1_out, a);
  not not_2 (not_2_out, b);
  not not_3 (not_3_out, c_in);
  and and_1 (and_1_out, not_1_out, not_2_out, c_in);
  and and_2 (and_2_out, not_1_out, b, not_3_out);
  and and_3 (and_3_out, a, not_2_out, not_3_out);
  and and_4 (and_4_out, a, b, c_in);
  and and_5 (and_5_out, b, c_in);
  and and_6 (and_6_out, a, c_in);
  and and_7 (and_7_out, a, b);
  or or_1 (s, and_1_out, and_2_out, and_3_out, and_4_out);
  or or_2 (c_out, and_5_out, and_6_out, and_7_out);
endmodule

module additionneur_4_bits (
  input  a0,
  input  a1,
  input  b0,
  input  b1,
  input  c_in,
  input  a2,
  input  b2,
  input  a3,
  input  b3,
  output s0,
  output s1,
  output s2,
  output s3,
  output c_out
);

  wire additionneur_complet_table_1_c_out, additionneur_complet_table_2_c_out,
       additionneur_complet_table_4_c_out;

  additionneur_complet_table additionneur_complet_table_1 (
    .a(a0), .b(b0), .c_in(c_in), .s(s0), .c_out(additionneur_complet_table_1_c_out));
  additionneur_complet_table additionneur_complet_table_2 (
    .a(a2), .b(b2), .c_in(additionneur_complet_table_4_c_out), .s(s2),
    .c_out(additionneur_complet_table_2_c_out));
  additionneur_complet_table additionneur_complet_table_3 (
    .a(a3), .b(b3), .c_in(additionneur_complet_table_2_c_out), .s(s3), .c_out(c_out));
  additionneur_complet_table additionneur_complet_table_4 (
    .a(a1), .b(b1), .c_in(additionneur_complet_table_1_c_out), .s(s1),
    .c_out(additionneur_complet_table_4_c_out));
endmodule

module additionneur_4_bits_aff (
  input  [3:0] A,
  input  c_in,
  input  [3:0] B,
  output c_out
);

  wire additionneur_4_bits_1_s0, additionneur_4_bits_1_s1, additionneur_4_bits_1_s2,
       additionneur_4_bits_1_s3, aff_hexa_1_a, aff_hexa_1_b, aff_hexa_1_c, aff_hexa_1_d, aff_hexa_1_e,
       aff_hexa_1_f, aff_hexa_1_g, aff_hexa_2_a, aff_hexa_2_b, aff_hexa_2_c, aff_hexa_2_d, aff_hexa_2_e,
       aff_hexa_2_f, aff_hexa_2_g, aff_hexa_3_a, aff_hexa_3_b, aff_hexa_3_c, aff_hexa_3_d, aff_hexa_3_e,
       aff_hexa_3_f, aff_hexa_3_g;

  additionneur_4_bits additionneur_4_bits_1 (
    .a0(A[0]), .a1(A[1]), .b0(B[0]), .b1(B[1]), .c_in(c_in), .a2(A[2]), .b2(B[2]), .a3(A[3]), .b3(B[3]),
    .s0(additionneur_4_bits_1_s0), .s1(additionneur_4_bits_1_s1), .s2(additionneur_4_bits_1_s2),
    .s3(additionneur_4_bits_1_s3), .c_out(c_out));
  aff_hexa aff_hexa_1 (
    .e0(A[0]), .e1(A[1]), .e2(A[2]), .e3(A[3]), .a(aff_hexa_1_a), .b(aff_hexa_1_b), .c(aff_hexa_1_c),
    .d(aff_hexa_1_d), .e(aff_hexa_1_e), .f(aff_hexa_1_f), .g(aff_hexa_1_g));
  aff_hexa aff_hexa_2 (
    .e0(B[0]), .e1(B[1]), .e2(B[2]), .e3(B[3]), .a(aff_hexa_2_a), .b(aff_hexa_2_b), .c(aff_hexa_2_c),
    .d(aff_hexa_2_d), .e(aff_hexa_2_e), .f(aff_hexa_2_f), .g(aff_hexa_2_g));
  _7_Segment_Display u_7_segment_display_1 (
    .g(aff_hexa_1_g), .f(aff_hexa_1_f), .a(aff_hexa_1_a), .b(aff_hexa_1_b), .e(aff_hexa_1_e),
    .d(aff_hexa_1_d), .c(aff_hexa_1_c));  // open: dp
  _7_Segment_Display u_7_segment_display_2 (
    .g(aff_hexa_2_g), .f(aff_hexa_2_f), .a(aff_hexa_2_a), .b(aff_hexa_2_b), .e(aff_hexa_2_e),
    .d(aff_hexa_2_d), .c(aff_hexa_2_c));  // open: dp
  aff_hexa aff_hexa_3 (
    .e0(additionneur_4_bits_1_s0), .e1(additionneur_4_bits_1_s1), .e2(additionneur_4_bits_1_s2),
    .e3(additionneur_4_bits_1_s3), .a(aff_hexa_3_a), .b(aff_hexa_3_b), .c(aff_hexa_3_c), .d(aff_hexa_3_d),
    .e(aff_hexa_3_e), .f(aff_hexa_3_f), .g(aff_hexa_3_g));
  _7_Segment_Display u_7_segment_display_3 (
    .g(aff_hexa_3_g), .f(aff_hexa_3_f), .a(aff_hexa_3_a), .b(aff_hexa_3_b), .e(aff_hexa_3_e),
    .d(aff_hexa_3_d), .c(aff_hexa_3_c));  // open: dp
endmodule

module aff_hexa (
  input  e0,
  input  e1,
  input  e2,
  input  e3,
  output a,
  output b,
  output c,
  output d,
  output e,
  output f,
  output g
);

  wire and_1_out, and_2_out, and_3_out, and_4_out, and_5_out, and_6_out, and_7_out, and_8_out, and_9_out,
       and_10_out, and_11_out, and_12_out, and_13_out, and_14_out, and_15_out, and_16_out, and_17_out,
       and_18_out, and_19_out, and_20_out, and_21_out, and_22_out, and_23_out, and_24_out, and_25_out,
       and_26_out, and_27_out, and_28_out, and_29_out, and_30_out, and_31_out, and_32_out, and_33_out,
       and_34_out, and_35_out, and_36_out, and_37_out, and_38_out, and_39_out, and_40_out, not_1_out,
       not_2_out, not_3_out, not_4_out;

  not not_1 (not_1_out, e0);
  not not_2 (not_2_out, e1);
  not not_3 (not_3_out, e2);
  not not_4 (not_4_out, e3);
  and and_1 (and_1_out, not_2_out, not_4_out);
  and and_2 (and_2_out, not_1_out, e2);
  and and_3 (and_3_out, not_1_out, e1, e3);
  and and_4 (and_4_out, e0, not_2_out, not_3_out);
  and and_5 (and_5_out, e0, not_4_out);
  and and_6 (and_6_out, e1, e2);
  and and_7 (and_7_out, not_1_out, not_3_out, not_4_out);
  and and_8 (and_8_out, not_1_out, e2, e3);
  and and_9 (and_9_out, not_2_out, not_4_out);
  and and_10 (and_10_out, e0, not_3_out, e3);
  and and_11 (and_11_out, not_1_out, not_2_out);
  and and_12 (and_12_out, not_1_out, e1);
  and and_13 (and_13_out, e0, not_2_out);
  and and_14 (and_14_out, not_3_out, e3);
  and and_15 (and_15_out, not_1_out, not_3_out);
  and and_16 (and_16_out, not_1_out, e3);
  and and_17 (and_17_out, e1, not_3_out, e3);
  and and_18 (and_18_out, not_1_out, not_2_out, not_4_out);
  and and_19 (and_19_out, not_1_out, not_2_out, e2);
  and and_20 (and_20_out, not_1_out, e2, not_4_out);
  and and_21 (and_21_out, not_2_out, not_3_out, not_4_out);
  and and_22 (and_22_out, e0, not_3_out);
  and and_23 (and_23_out, not_2_out, e2, e3);
  and and_24 (and_24_out, e1, e2, not_4_out);
  and and_25 (and_25_out, not_2_out, not_4_out);
  and and_26 (and_26_out, e2, not_4_out);
  and and_27 (and_27_out, e0, e2);
  and and_28 (and_28_out, e0, e1);
  and and_29 (and_29_out, not_3_out, not_4_out);
  and and_30 (and_30_out, not_1_out, e1, not_3_out);
  and and_31 (and_31_out, e1, not_4_out);
  and and_32 (and_32_out, e0, not_2_out);
  and and_33 (and_33_out, e0, e2);
  and and_34 (and_34_out, not_2_out, e2);
  and and_35 (and_35_out, e0, not_2_out);
  and and_36 (and_36_out, not_1_out, e1, not_3_out);
  and and_37 (and_37_out, not_1_out, e1, not_4_out);
  and and_38 (and_38_out, e1, not_3_out, e3);
  and and_39 (and_39_out, e2, not_4_out);
  and and_40 (and_40_out, e0, e3);
  or or_1 (a, and_1_out, and_2_out, and_3_out, and_4_out, and_5_out, and_6_out);
  or or_2 (b, and_7_out, and_8_out, and_9_out, and_10_out, and_11_out);
  or or_3 (c, and_12_out, and_13_out, and_14_out, and_15_out, and_16_out);
  or or_4 (d, and_17_out, and_18_out, and_19_out, and_20_out, and_21_out, and_22_out, and_23_out, and_24_out);
  or or_5 (e, and_25_out, and_26_out, and_27_out, and_28_out);
  or or_6 (f, and_29_out, and_30_out, and_31_out, and_32_out, and_33_out);
  or or_7 (g, and_34_out, and_35_out, and_36_out, and_37_out, and_38_out, and_39_out, and_40_out);
endmodule
