// Logisim project TP4.circ as structural Verilog
module Decodeur (
  input  e0,
  input  e1,
  output s0,
  output s1,
  output s2,
  output s3
);

  wire not_1_out, not_2_out;

  not not_1 (not_1_out, e0);
  not not_2 (not_2_out, e1);
  and and_1 (s0, not_1_out, not_2_out);
  and and_2 (s1, not_2_out, e0);
  and and_3 (s2, e1, not_1_out);
  and and_4 (s3, e0, e1);
endmodule

module Multiplexeur (
  input  e0,
  input  e1,
  input  e2,
  input  e3,
  input  a0,
  input  a1,
  output s
);

  wire and_1_out, and_2_out, and_3_out, and_4_out, decodeur_1_s0, decodeur_1_s1, decodeur_1_s2, decodeur_1_s3;

  Decodeur decodeur_1 (
    .e0(a0), .e1(a1), .s0(decodeur_1_s0), .s1(decodeur_1_s1), .s2(decodeur_1_s2), .s3(decodeur_1_s3));
  and and_1 (and_1_out, e0, decodeur_1_s0);
  and and_2 (and_2_out, e1, decodeur_1_s1);
  and and_3 (and_3_out, e2, decodeur_1_s2);
  and and_4 (and_4_out, e3, decodeur_1_s3);
  or or_1 (s, and_1_out, and_2_out, and_3_out, and_4_out);
endmodule

module UAL_1_bit (
  input  a,
  input  b,
  input  c_in,
  input  s0,
  input  s1,
  output f,
  output c_out
);

  wire and_1_out, full_add_1_s, not_1_out, or_1_out;

  not not_1 (not_1_out, a);
  or or_1 (or_1_out, a, b);
  and and_1 (and_1_out, a, c_in);
  full_add full_add_1 (.A(a), .B(b), .c_in(c_in), .S(full_add_1_s), .C_out(c_out));
  Multiplexeur multiplexeur_1 (
    .e0(not_1_out), .e1(or_1_out), .e2(and_1_out), .e3(full_add_1_s), .a0(s0), .a1(s1), .s(f));
endmodule

module full_add (
  input  A,
  input  B,
  input  c_in,
  output S,
  output C_out
);

  wire and_1_out, and_2_out, xor_1_out;

  xor xor_1 (xor_1_out, A, B);
  and and_1 (and_1_out, A, B);
  xor xor_2 (S, xor_1_out, c_in);
  and and_2 (and_2_out, xor_1_out, c_in);
  or or_1 (C_out, and_2_out, and_1_out);
endmodule

module UAL_4_bits (
  input  a0,
  input  b0,
  input  c_in,
  input  s0,
  input  s1,
  input  a1,
  input  b1,
  input  a2,
  input  b2,
  input  a3,
  input  b3,
  output f0,
  output C,
  output f1,
  output Z,
  output f2,
  output V,
  output f3,
  output N,
  output c_out
);

  wire or_1_out, ual_1_bit_1_c_out, ual_1_bit_2_c_out, ual_1_bit_3_c_out;

  UAL_1_bit ual_1_bit_1 (.a(a0), .b(b0), .c_in(c_in), .s0(s0), .s1(s1), .f(f0), .c_out(ual_1_bit_1_c_out));
  UAL_1_bit ual_1_bit_2 (.a(a1), .b(b1), .c_in(ual_1_bit_1_c_out), .s0(s0), .s1(s1), .f(f1), .c_out(ual_1_bit_2_c_out));
  UAL_1_bit ual_1_bit_3 (.a(a2), .b(b2), .c_in(ual_1_bit_2_c_out), .s0(s0), .s1(s1), .f(f2), .c_out(ual_1_bit_3_c_out));
  UAL_1_bit ual_1_bit_4 (.a(a3), .b(b3), .c_in(ual_1_bit_3_c_out), .s0(s0), .s1(s1), .f(f3), .c_out(c_out));
  xor xor_1 (V, ual_1_bit_3_c_out, c_out);
  or or_1 (or_1_out, f0, f1, f2, f3);
  not not_1 (Z, or_1_out);
  xor xor_2 (C, c_in, c_out);

  assign N = f3;
endmodule
