// Logisim project TP5.circ as structural Verilog
module aff_hexa (
  input  e3,
  input  e2,
  input  e1,
  input  e0,
  output a,
  output b,
  output c,
  output d,
  output e,
  output f,
  output g
);

  wire and_1_out, and_2_out, and_3_out, and_4_out, and_5_out, and_6_out, and_7_out, and_8_out, and_9_out,
       and_10_out, and_11_out, and_12_out, and_13_out, and_14_out, and_15_out, and_16_out, and_17_out,
       and_18_out, and_19_out, and_20_out, and_21_out, and_22_out, and_23_out, and_24_out, and_25_out,
       and_26_out, and_27_out, and_28_out, and_29_out, and_30_out, and_31_out, and_32_out, and_33_out,
       and_34_out, and_35_out, not_1_out, not_2_out, not_3_out, not_4_out;

  not not_1 (not_1_out, e3);
  not not_2 (not_2_out, e2);
  not not_3 (not_3_out, e1);
  not not_4 (not_4_out, e0);
  and and_1 (and_1_out, not_2_out, not_4_out);
  and and_2 (and_2_out, not_1_out, e1);
  and and_3 (and_3_out, not_1_out, e2, e0);
  and and_4 (and_4_out, e3, not_2_out, not_3_out);
  and and_5 (and_5_out, e3, not_4_out);
  and and_6 (and_6_out, e2, e1);
  and and_7 (and_7_out, not_1_out, not_3_out, not_4_out);
  and and_8 (and_8_out, not_1_out, e1, e0);
  and and_9 (and_9_out, not_2_out, not_4_out);
  and and_10 (and_10_out, e3, not_3_out, e0);
  and and_11 (and_11_out, not_1_out, not_2_out);
  and and_12 (and_12_out, not_1_out, e2);
  and and_13 (and_13_out, e3, not_2_out);
  and and_14 (and_14_out, not_3_out, e0);
  and and_15 (and_15_out, not_2_out, not_3_out);
  and and_16 (and_16_out, not_2_out, e0);
  and and_17 (and_17_out, e2, not_3_out, e0);
  and and_18 (and_18_out, not_1_out, not_2_out, not_4_out);
  and and_19 (and_19_out, not_2_out, e1, e0);
  and and_20 (and_20_out, e3, not_3_out);
  and and_21 (and_21_out, e2, e1, not_4_out);
  and and_22 (and_22_out, not_2_out, not_4_out);
  and and_23 (and_23_out, e1, not_4_out);
  and and_24 (and_24_out, e3, e1);
  and and_25 (and_25_out, e3, e2);
  and and_26 (and_26_out, not_3_out, not_4_out);
  and and_27 (and_27_out, not_1_out, e2, not_3_out);
  and and_28 (and_28_out, e2, not_4_out);
  and and_29 (and_29_out, e3, not_2_out);
  and and_30 (and_30_out, e3, e1);
  and and_31 (and_31_out, not_2_out, e1);
  and and_32 (and_32_out, e3, not_2_out);
  and and_33 (and_33_out, not_1_out, e2, not_3_out);
  and and_34 (and_34_out, e1, not_4_out);
  and and_35 (and_35_out, e3, e0);
  or or_1 (a, and_1_out, and_2_out, and_3_out, and_4_out, and_5_out, and_6_out);
  or or_2 (b, and_7_out, and_8_out, and_9_out, and_10_out, and_11_out);
  or or_3 (c, and_12_out, and_13_out, and_14_out, and_15_out, and_16_out);
  or or_4 (d, and_17_out, and_18_out, and_19_out, and_20_out, and_21_out);
  or or_5 (e, and_22_out, and_23_out, and_24_out, and_25_out);
  or or_6 (f, and_26_out, and_27_out, and_28_out, and_29_out, and_30_out);
  or or_7 (g, and_31_out, and_32_out, and_33_out, and_34_out, and_35_out);
endmodule

module Horloge (
  output H0,
  output H1,
  output H2,
  output H3
);

  Clock clock_1 (.out(H0));
  Clock #(.highDuration(2), .lowDuration(2)) clock_2 (.out(H1));
  Clock #(.highDuration(4), .lowDuration(4)) clock_3 (.out(H2));
  Clock #(.highDuration(8), .lowDuration(8)) clock_4 (.out(H3));
endmodule

module horloge_aff_hexa (
);

  wire aff_hexa_1_a, aff_hexa_1_b, aff_hexa_1_c, aff_hexa_1_d, aff_hexa_1_e, aff_hexa_1_f, aff_hexa_1_g,
       horloge_1_h0, horloge_1_h1, horloge_1_h2, horloge_1_h3;

  Horloge horloge_1 (.H0(horloge_1_h0), .H1(horloge_1_h1), .H2(horloge_1_h2), .H3(horloge_1_h3));
  aff_hexa aff_hexa_1 (
    .e3(horloge_1_h0), .e2(horloge_1_h1), .e1(horloge_1_h2), .e0(horloge_1_h3), .a(aff_hexa_1_a),
    .b(aff_hexa_1_b), .c(aff_hexa_1_c), .d(aff_hexa_1_d), .e(aff_hexa_1_e), .f(aff_hexa_1_f), .g(aff_hexa_1_g));
  _7_Segment_Display u_7_segment_display_1 (
    .g(aff_hexa_1_g), .f(aff_hexa_1_f), .a(aff_hexa_1_a), .b(aff_hexa_1_b), .e(aff_hexa_1_e),
    .d(aff_hexa_1_d), .c(aff_hexa_1_c));  // open: dp
endmodule

module Bascules (
  input  Pr,
  input  Pr1,
  input  R,
  input  J,
  input  S,
  input  K,
  input  Cr,
  input  Cr1,
  input  Pr2,
  input  Pr3,
  input  D,
  input  T,
  input  Cr2,
  input  Cr3,
  output Q0,
  output Q1,
  output Q0_bar,
  output Q1_bar,
  output Q2,
  output Q3,
  output Q2_bar,
  output Q3_bar
);

  wire H0_out, H1_out, H2_out, H3_out;

  Clock H0 (.out(H0_out));
  Clock H2 (.out(H2_out));
  S_R_Flip_Flop s_r_ff_1 (.S(S), .R(R), .clk(H0_out), .Q(Q0), .reset(Cr), .Qn(Q0_bar), .preset(Pr));
  D_Flip_Flop d_ff_1 (.D(D), .clk(H2_out), .Q(Q2), .Qn(Q2_bar), .preset(Pr2), .reset(Cr2));
  Clock H1 (.out(H1_out));
  Clock H3 (.out(H3_out));
  J_K_Flip_Flop j_k_ff_1 (.J(J), .K(K), .clk(H1_out), .Q(Q1), .Qn(Q1_bar), .preset(Pr1), .reset(Cr1));
  T_Flip_Flop t_ff_1 (.T(T), .clk(H3_out), .Q(Q3), .Qn(Q3_bar), .reset(Cr3), .preset(Pr3));

  // Notes on the sheet:
  //   BASCULE RS
  //   BASCULE D
  //   BASCULE T
  //   BASCULE JK
endmodule

module registre_decalage_gauche (
  input  E,
  output Q0,
  output Q1,
  output Q2,
  output Q3
);

  wire H_out;

  Clock H (.out(H_out));
  D_Flip_Flop d_ff_1 (.D(E), .clk(H_out), .Q(Q0));  // open: Qn, preset, reset
  D_Flip_Flop d_ff_2 (.D(Q0), .clk(H_out), .Q(Q1));  // open: Qn, preset, reset
  D_Flip_Flop d_ff_3 (.D(Q1), .clk(H_out), .Q(Q2));  // open: Qn, preset, reset
  D_Flip_Flop d_ff_4 (.D(Q2), .clk(H_out), .Q(Q3));  // open: Qn, preset, reset
endmodule

module registre_decalage_droite (
  input  E,
  output Q0,
  output Q1,
  output Q2,
  output Q3
);

  wire H_out;

  Clock H (.out(H_out));
  D_Flip_Flop d_ff_1 (.D(Q1), .clk(H_out), .Q(Q0));  // open: Qn, preset, reset
  D_Flip_Flop d_ff_2 (.D(Q2), .clk(H_out), .Q(Q1));  // open: Qn, preset, reset
  D_Flip_Flop d_ff_3 (.D(Q3), .clk(H_out), .Q(Q2));  // open: Qn, preset, reset
  D_Flip_Flop d_ff_4 (.D(E), .clk(H_out), .Q(Q3));  // open: Qn, preset, reset
endmodule

module registre_decalage_G_D (
  input  G_D,
  input  E,
  output Q0,
  output Q1,
  output Q2,
  output Q3
);

  wire H_out, multiplexer_1_out, multiplexer_2_out, multiplexer_3_out, multiplexer_4_out;

  Clock H (.out(H_out));
  D_Flip_Flop d_ff_1 (.D(multiplexer_1_out), .clk(H_out), .Q(Q0));  // open: Qn, preset, reset
  Multiplexer multiplexer_1 (.in1(E), .out(multiplexer_1_out), .sel(G_D));  // open: in0
  Multiplexer multiplexer_2 (.in0(Q1), .in1(Q0), .out(multiplexer_2_out), .sel(G_D));
  D_Flip_Flop d_ff_2 (.D(multiplexer_2_out), .clk(H_out), .Q(Q1));  // open: Qn, preset, reset
  Multiplexer multiplexer_3 (.in0(Q2), .in1(Q1), .out(multiplexer_3_out), .sel(G_D));
  D_Flip_Flop d_ff_3 (.D(multiplexer_3_out), .clk(H_out), .Q(Q2));  // open: Qn, preset, reset
  Multiplexer multiplexer_4 (.in0(Q3), .in1(Q2), .out(multiplexer_4_out), .sel(G_D));
  D_Flip_Flop d_ff_4 (.D(multiplexer_4_out), .clk(H_out), .Q(Q3));  // open: Qn, preset, reset
endmodule
