// Logisim project TP6.circ as structural Verilog: 5 circuits, main circuit registre_1bit
module registre_1bit (
  input  e,
  input  R,
  input  EN,
  output S
);

  wire and_1_out, d_ff_1_q, W_out;

  Clock W (.out(W_out));
  and and_1 (and_1_out, W_out, EN);
  D_Flip_Flop d_ff_1 (.D(e), .clk(and_1_out), .Q(d_ff_1_q));  // open: Qn, preset, reset
  and and_2 (S, R, EN, d_ff_1_q);
endmodule

module registre_4bits (
  input  e,
  input  R,
  input  EN,
  output out_4,
  output out_5,
  output out_6,
  output out_7
);

  registre_1bit registre_1bit_1 (.e(e), .R(R), .EN(EN), .S(out_5));
  registre_1bit registre_1bit_2 (.e(out_5), .R(R), .EN(EN), .S(out_6));
  registre_1bit registre_1bit_3 (.e(out_6), .R(R), .EN(EN), .S(out_7));
  registre_1bit registre_1bit_4 (.e(out_7), .R(R), .EN(EN), .S(out_4));
endmodule

module registre_8mots (
  input  EN,
  input  R,
  input  a2,
  input  a1,
  input  a0,
  output [3:0] out_6,
  output [3:0] out_7,
  output [3:0] out_8,
  output [3:0] out_9,
  output [3:0] out_10,
  output [3:0] out_11,
  output [3:0] out_12,
  output [3:0] out_13
);

  wire decodeur_1_s0, decodeur_1_s1, decodeur_1_s2, decodeur_1_s3, decodeur_1_s4, decodeur_1_s5,
       decodeur_1_s6, decodeur_1_s7;

  decodeur decodeur_1 (
    .a2(a2), .a1(a1), .a0(a0), .S7(decodeur_1_s7), .S6(decodeur_1_s6), .S5(decodeur_1_s5),
    .S4(decodeur_1_s4), .S3(decodeur_1_s3), .S2(decodeur_1_s2), .S1(decodeur_1_s1), .S0(decodeur_1_s0));
  registre_4bits registre_4bits_1 (
    .e(decodeur_1_s7), .R(R), .EN(EN), .out_4(out_6[0]), .out_5(out_6[1]), .out_6(out_6[2]), .out_7(out_6[3]));
  registre_4bits registre_4bits_2 (
    .e(decodeur_1_s6), .R(R), .EN(EN), .out_4(out_7[0]), .out_5(out_7[1]), .out_6(out_7[2]), .out_7(out_7[3]));
  registre_4bits registre_4bits_3 (
    .e(decodeur_1_s5), .R(R), .EN(EN), .out_4(out_8[0]), .out_5(out_8[1]), .out_6(out_8[2]), .out_7(out_8[3]));
  registre_4bits registre_4bits_4 (
    .e(decodeur_1_s4), .R(R), .EN(EN), .out_4(out_9[0]), .out_5(out_9[1]), .out_6(out_9[2]), .out_7(out_9[3]));
  registre_4bits registre_4bits_5 (
    .e(decodeur_1_s3), .R(R), .EN(EN), .out_4(out_10[0]), .out_5(out_10[1]), .out_6(out_10[2]),
    .out_7(out_10[3]));
  registre_4bits registre_4bits_6 (
    .e(decodeur_1_s2), .R(R), .EN(EN), .out_4(out_11[0]), .out_5(out_11[1]), .out_6(out_11[2]),
    .out_7(out_11[3]));
  registre_4bits registre_4bits_7 (
    .e(decodeur_1_s1), .R(R), .EN(EN), .out_4(out_12[0]), .out_5(out_12[1]), .out_6(out_12[2]),
    .out_7(out_12[3]));
  registre_4bits registre_4bits_8 (
    .e(decodeur_1_s0), .R(R), .EN(EN), .out_4(out_13[0]), .out_5(out_13[1]), .out_6(out_13[2]),
    .out_7(out_13[3]));
endmodule

module decodeur (
  input  a2,
  input  a1,
  input  a0,
  output S7,
  output S6,
  output S5,
  output S4,
  output S3,
  output S2,
  output S1,
  output S0
);

  wire not_1_out, not_2_out, not_3_out;

  not not_1 (not_1_out, a2);
  not not_2 (not_2_out, a1);
  not not_3 (not_3_out, a0);
  and and_1 (S7, a2, a1, a0);
  and and_2 (S6, a2, a1, not_3_out);
  and and_3 (S5, a2, not_2_out, a0);
  and and_4 (S4, a2, not_2_out, not_3_out);
  and and_5 (S3, not_1_out, a1, a0);
  and and_6 (S2, not_1_out, a1, not_3_out);
  and and_7 (S1, not_1_out, not_2_out, a0);
  and and_8 (S0, not_1_out, not_2_out, not_3_out);
endmodule

module registre_32mots (
  output out_1
);

  registre_8mots registre_8mots_1 ();  // open: EN, R, a2, a1, a0, out_6, out_7, out_8, out_9, out_10, out_11, out_12, out_13
  registre_8mots registre_8mots_2 ();  // open: EN, R, a2, a1, a0, out_6, out_7, out_8, out_9, out_10, out_11, out_12, out_13
  registre_8mots registre_8mots_3 ();  // open: EN, R, a2, a1, a0, out_6, out_7, out_8, out_9, out_10, out_11, out_12, out_13
  registre_8mots registre_8mots_4 ();  // open: EN, R, a2, a1, a0, out_6, out_7, out_8, out_9, out_10, out_11, out_12, out_13
endmodule
