// Logisim project tp7(2).circ as structural Verilog: 5 circuits, main circuit compteur_0_15
module compteur_0_15 (
  output Q0,
  output Q1,
  output Q2,
  output Q3
);

  wire H_out, j_k_ff_1_q, j_k_ff_2_q, j_k_ff_3_q, j_k_ff_4_q;

  Clock H (.out(H_out));
  J_K_Flip_Flop j_k_ff_1 (.J(1'b1), .K(1'b1), .clk(H_out), .Q(j_k_ff_1_q));  // open: Qn, preset, reset
  not not_1 (Q0, j_k_ff_1_q);
  not not_2 (Q1, j_k_ff_2_q);
  J_K_Flip_Flop j_k_ff_2 (.J(1'b1), .K(1'b1), .clk(j_k_ff_1_q), .Q(j_k_ff_2_q));  // open: Qn, preset, reset
  J_K_Flip_Flop j_k_ff_3 (.J(1'b1), .K(1'b1), .clk(j_k_ff_2_q), .Q(j_k_ff_3_q));  // open: Qn, preset, reset
  not not_3 (Q2, j_k_ff_3_q);
  J_K_Flip_Flop j_k_ff_4 (.J(1'b1), .K(1'b1), .clk(j_k_ff_3_q), .Q(j_k_ff_4_q));  // open: Qn, preset, reset
  not not_4 (Q3, j_k_ff_4_q);
  Hex_Digit_Display hex_digit_display_1 (.value({Q3, Q2, Q1, Q0}));  // open: dp
endmodule

module compteur_0_9 (
  output Q0,
  output Q1,
  output Q2,
  output Q3
);

  wire and_1_out, H_out, j_k_ff_1_q, j_k_ff_2_q, j_k_ff_3_q, j_k_ff_4_q, undriven, undriven_2, undriven_3,
       undriven_4;

  Clock H (.out(H_out));
  J_K_Flip_Flop j_k_ff_1 (
    .J(1'b1), .K(1'b1), .clk(H_out), .Q(j_k_ff_1_q), .preset(and_1_out), .reset(undriven));  // open: Qn
  not not_1 (Q0, j_k_ff_1_q);
  not not_2 (Q1, j_k_ff_2_q);
  J_K_Flip_Flop j_k_ff_2 (
    .J(1'b1), .K(1'b1), .clk(j_k_ff_1_q), .Q(j_k_ff_2_q), .preset(and_1_out), .reset(undriven_2));  // open: Qn
  J_K_Flip_Flop j_k_ff_3 (
    .J(1'b1), .K(1'b1), .clk(j_k_ff_2_q), .Q(j_k_ff_3_q), .preset(and_1_out), .reset(undriven_3));  // open: Qn
  not not_3 (Q2, j_k_ff_3_q);
  J_K_Flip_Flop j_k_ff_4 (
    .J(1'b1), .K(1'b1), .clk(j_k_ff_3_q), .Q(j_k_ff_4_q), .preset(and_1_out), .reset(undriven_4));  // open: Qn
  not not_4 (Q3, j_k_ff_4_q);
  and and_1 (and_1_out, Q1, Q3);
  Hex_Digit_Display hex_digit_display_1 (.value({Q3, Q2, Q1, Q0}));  // open: dp
endmodule

module Compteur_0_5 (
  input  in_1,
  output Q2,
  output Q0,
  output Q1,
  output Q3
);

  wire and_1_out, and_2_out, and_3_out, and_4_out, clock_1_out, not_1_out, not_2_out, not_3_out, or_1_out,
       or_2_out;

  D_Flip_Flop d_ff_1 (.D(not_1_out), .clk(clock_1_out), .Q(Q0));  // open: Qn, preset, reset
  Clock clock_1 (.out(clock_1_out));
  not not_1 (not_1_out, Q0);
  and and_1 (and_1_out, Q0, not_2_out, not_3_out);
  and and_2 (and_2_out, not_1_out, Q1);
  or or_1 (or_1_out, and_1_out, and_2_out);
  and and_3 (and_3_out, Q1, Q0);
  and and_4 (and_4_out, not_1_out, Q2);
  D_Flip_Flop d_ff_2 (.D(or_1_out), .clk(clock_1_out), .Q(Q1));  // open: Qn, preset, reset
  or or_2 (or_2_out, and_3_out, and_4_out);
  not not_2 (not_2_out, Q1);
  D_Flip_Flop d_ff_3 (.D(or_2_out), .clk(clock_1_out), .Q(Q2));  // open: Qn, preset, reset
  not not_3 (not_3_out, Q2);
  D_Flip_Flop d_ff_4 (.D(in_1), .clk(clock_1_out), .Q(Q3));  // open: Qn, preset, reset
  Hex_Digit_Display hex_digit_display_1 (.value({Q3, Q2, Q1, Q0}));  // open: dp
endmodule

module Transcodeur (
  input  in_1,
  input  in_2,
  output Q2,
  output Q0,
  output Q1,
  output S2,
  output S3,
  output S1,
  output S0
);

  wire and_1_out, and_2_out, and_3_out, and_4_out, and_5_out, clock_1_out, d_ff_1_qn, not_1_out, not_2_out,
       not_3_out, or_1_out, or_2_out;

  D_Flip_Flop d_ff_1 (.D(not_1_out), .clk(clock_1_out), .Q(Q0), .Qn(d_ff_1_qn));  // open: preset, reset
  Clock clock_1 (.out(clock_1_out));
  not not_1 (not_1_out, Q0);
  and and_1 (and_1_out, Q0, not_2_out, not_3_out);
  and and_2 (and_2_out, not_1_out, Q1);
  or or_1 (or_1_out, and_1_out, and_2_out);
  and and_3 (and_3_out, Q1, Q0);
  and and_4 (and_4_out, not_1_out, Q2);
  D_Flip_Flop d_ff_2 (.D(or_1_out), .clk(clock_1_out), .Q(Q1));  // open: Qn, preset, reset
  or or_2 (or_2_out, and_3_out, and_4_out);
  and and_5 (and_5_out, d_ff_1_qn, Q1);
  not not_2 (not_2_out, Q1);
  or or_3 (S1, Q2, and_5_out);
  D_Flip_Flop d_ff_3 (.D(or_2_out), .clk(clock_1_out), .Q(Q2));  // open: Qn, preset, reset
  not not_3 (not_3_out, Q2);
  Hex_Digit_Display hex_digit_display_1 (.value({in_2, in_1, S1, Q0}));  // open: dp

  assign S0 = Q0;
  assign S2 = in_1;
  assign S3 = in_2;
endmodule

module trancodeur_BIT_LOAD (
  input  in_1,
  input  [2:0] E,
  input  LOAD,
  output Q1,
  output Q2,
  output Q0,
  output Q3
);

  wire and_1_out, and_2_out, and_3_out, and_4_out, clock_1_out, not_2_out, not_3_out;
  wire [2:0] multiplexer_1_out, not_1_out;

  not not_1 (not_1_out[0], Q0);
  D_Flip_Flop d_ff_1 (.D(multiplexer_1_out[0]), .clk(clock_1_out), .Q(Q0));  // open: Qn, preset, reset
  Clock clock_1 (.out(clock_1_out));
  and and_1 (and_1_out, Q0, not_2_out, not_3_out);
  and and_2 (and_2_out, not_1_out[0], Q1);
  Multiplexer #(.width(3)) multiplexer_1 (.in0(not_1_out), .in1(E), .out(multiplexer_1_out), .sel(LOAD));
  or or_1 (not_1_out[1], and_1_out, and_2_out);
  and and_3 (and_3_out, Q1, Q0);
  and and_4 (and_4_out, not_1_out[0], Q2);
  D_Flip_Flop d_ff_2 (.D(multiplexer_1_out[1]), .clk(clock_1_out), .Q(Q1));  // open: Qn, preset, reset
  or or_2 (not_1_out[2], and_3_out, and_4_out);
  not not_2 (not_2_out, Q1);
  D_Flip_Flop d_ff_3 (.D(multiplexer_1_out[2]), .clk(clock_1_out), .Q(Q2));  // open: Qn, preset, reset
  not not_3 (not_3_out, Q2);
  D_Flip_Flop d_ff_4 (.D(in_1), .clk(clock_1_out), .Q(Q3));  // open: Qn, preset, reset
  Hex_Digit_Display hex_digit_display_1 (.value({Q3, Q2, Q1, Q0}));  // open: dp
endmodule
